# Fritzing sketch nRFBox (saved by Fritzing 1.0.1rc)
circuit board: 10cm x 5.64cm
breadboards: 1

parts:
  U1 = ESP32S-HiLetgo [part_number=ESP32S-HiLetgo]
  UP = Pushbutton [package="[THT]"]
  DOWN = Pushbutton [package="[THT]"]
  SELECT = Pushbutton [package="[THT]"]
  LEFT = Pushbutton [package="[THT]"]
  RIGHT = Pushbutton [package="[THT]"]
  OLED_I2C1 = OLED 128x64 I2C Monochrome Display
  RF1 = NRF24L01+ Breakout Board
  RF2 = NRF24L01+ Breakout Board
  RF3 = NRF24L01+ Breakout Board

nets:
  VCC: U1.3.3, OLED_I2C1.VDD, RF1.VCC, RF2.VCC, RF3.VCC
  N1: U1.GPIO32, DOWN.Pin_3, DOWN.Pin_4
  N2: U1.GPIO33, SELECT.Pin_3, SELECT.Pin_4
  N3: U1.GPIO25, LEFT.Pin_3, LEFT.Pin_4
  N4: U1.GPIO26, UP.Pin_3, UP.Pin_4
  N5: U1.GPIO27, RIGHT.Pin_3, RIGHT.Pin_4
  GND: U1.GND, OLED_I2C1.GND, RF1.GND, RF2.GND, RF3.GND
  N6: U1.GPIO15, RF2.CE
  N7: U1.GPIO2, RF2.CS
  N8: U1.GPIO4, RF1.CS
  N9: U1.GPIO16, RF1.CE
  N10: U1.GPIO17, RF3.CS
  N11: U1.GPIO5, RF3.CE
  N12: U1.GPIO18, RF1.SCK, RF2.SCK, RF3.SCK
  N13: U1.GPIO19, RF1.MISO, RF2.MISO, RF3.MISO
  N14: U1.GPIO21, OLED_I2C1.SDA
  N15: U1.GPIO22, OLED_I2C1.SCK
  N16: U1.GPIO23, RF1.MOSI, RF2.MOSI, RF3.MOSI
  N17: UP.Pin_1, UP.Pin_2, DOWN.Pin_1, DOWN.Pin_2, SELECT.Pin_1, SELECT.Pin_2, LEFT.Pin_1, LEFT.Pin_2, RIGHT.Pin_1, RIGHT.Pin_2

custom parts:
  ESP32S-HiLetgo: HiLetgo ESP-WROOM-32 ESP32 ESP-32S Development Board 2.4GHz Dual-Mode WiFi + Bluetooth Dual Cores Microcontroller The ESP32 integrated with Antenna switches, RF Balun, power amplifiers, low-noise amplifiers, filters, and management modules, and the entire solution occupies the least area of PCB. 2.4 GHz Wi-Fi plus Bluetooth dual-mode chip, with TSMC Ultra-low power consumption 40nm technology,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
